# Fritzing sketch yaorong_payment (saved by Fritzing 1.0.4)
breadboards: 1

parts:
  Part1 = Arduino Uno (Rev3)
  Part3 = RFID-RC522-v2

nets:
  N1: Part1.D9_PWM, Part3.RST
  N2: Part1.D10_PWM/SS, Part3.SDA
  N3: Part1.D11_PWM/MOSI, Part3.MOSI
  N4: Part1.D12/MISO, Part3.MISO
  N5: Part1.D13/SCK, Part3.SCK
  3V3: Part1.3V3, Part3.3.3V
  GND: Part1.GND, Part3.GND

custom parts:
  RFID-RC522-v2: A simple China made RFID-RC522 Reader; do check the pin labels, as this is a MFRC522 based clone.
